// Logisim project 1x8_demux_project.circ as structural Verilog: 2 circuits, main circuit main
module main (
  input  Selector0,
  input  Selector1,
  input  Selector2,
  input  Data_input,
  output Y0_out,
  output Y1_out,
  output Y2_out,
  output Y3_out,
  output Y4_out,
  output Y5_out,
  output Y6_out,
  output Y7_out
);

  demux demux_1x8 (
    .S2(Selector0), .S1(Selector1), .S0(Selector2), .D(Data_input), .Y0(Y0_out), .Y1(Y1_out), .Y2(Y2_out),
    .Y3(Y3_out), .Y4(Y4_out), .Y5(Y5_out), .Y6(Y6_out), .Y7(Y7_out));
endmodule

module demux (
  input  S2,
  input  S1,
  input  S0,
  input  D,
  output Y0,
  output Y1,
  output Y2,
  output Y3,
  output Y4,
  output Y5,
  output Y6,
  output Y7
);

  wire not_1_out, not_2_out, not_3_out;

  not not_1 (not_1_out, S2);
  not not_2 (not_2_out, S1);
  not not_3 (not_3_out, S0);
  and and_1 (Y0, not_3_out, not_2_out, not_1_out, D);
  and and_2 (Y1, not_3_out, not_2_out, S2, D);
  and and_3 (Y2, not_3_out, S1, not_1_out, D);
  and and_4 (Y3, not_3_out, S1, S2, D);
  and and_5 (Y4, S0, not_2_out, not_1_out, D);
  and and_6 (Y5, S0, not_2_out, S2, D);
  and and_7 (Y6, S0, S1, not_1_out, D);
  and and_8 (Y7, S0, S1, S2, D);
endmodule
